// Logisim project NSU-2023-T04L1e03.circ as structural Verilog: 1 circuit, main circuit mycircuit
module mycircuit (
  input  A,
  input  B,
  input  R,
  input  C
);

  nor nor_1 (R, B, C);
endmodule
