// Logisim project NSU-2023-T04L1e05.circ as structural Verilog: 1 circuit, main circuit mycircuit
module mycircuit (
  input  A,
  input  B,
  input  C,
  output R
);

  nand nand_1 (R, A, B, C);
endmodule
