// Logisim project NSU-2023-T04L1e06.circ as structural Verilog: 1 circuit, main circuit mycircuit
module mycircuit (
  input  A,
  input  B,
  input  R,
  input  C
);

  xnor xnor_1 (R, A, B);
endmodule
