// Logisim project NSU-2023-T04L1e12.circ as structural Verilog: 1 circuit, main circuit mycircuit
module mycircuit (
  input  A,
  input  B,
  input  C,
  output R
);

  wire not_1_out;

  not not_1 (not_1_out, B);
  or or_1 (R, A, not_1_out);
endmodule
