// Logisim project NSU-2023-T04L2e02.circ as structural Verilog: 1 circuit, main circuit formula
module formula (
  input  A,
  input  B,
  input  C,
  output R
);

  wire transistor_1_out;

  Transistor #(.\type ("n")) transistor_1 (.in(1'b0), .out(transistor_1_out), .gate(B));
  Transistor #(.\type ("n")) transistor_2 (.in(1'b0), .out(transistor_1_out), .gate(C));
  Pull_Resistor #(.pull(1)) pull_resistor_1 (.node(R));
  Transistor #(.\type ("n")) transistor_3 (.in(transistor_1_out), .out(R), .gate(A));

  // Notes on the sheet:
  //   R: pull=up
endmodule
