// Logisim project NSU-2023-T04L3e01.circ as structural Verilog: 1 circuit, main circuit formula
module formula (
  input  A,
  input  B,
  input  C,
  output R
);

  wire transistor_1_out, transistor_2_out;

  Transistor #(.\type ("n")) transistor_1 (.in(1'b0), .out(transistor_1_out), .gate(B));
  Transistor #(.\type ("n")) transistor_2 (.in(1'b0), .out(transistor_2_out), .gate(A));
  Transistor #(.\type ("n")) transistor_3 (.in(1'b0), .out(transistor_2_out), .gate(B));
  Transistor #(.\type ("n")) transistor_4 (.in(transistor_1_out), .out(R), .gate(A));
  Transistor #(.\type ("n")) transistor_5 (.in(transistor_2_out), .out(R), .gate(C));
  Pull_Resistor #(.pull(1)) pull_resistor_1 (.node(R));
endmodule
