// Logisim project NSU-2023-T05L2e02.circ as structural Verilog: 1 circuit, main circuit main
module main (
  input  [7:0] A,
  input  [7:0] B,
  output [7:0] sum,
  output Cout
);

  wire [6:0] or_1_out;
  wire [7:0] and_1_out, and_2_out, and_3_out;

  // Probe on A
  // Probe on B
  assign and_1_out = A & B;  // AND_Gate and_1, 8 bits wide
  assign and_2_out = B & {or_1_out, 1'b0};  // AND_Gate and_2, 8 bits wide
  assign and_3_out = A & {or_1_out, 1'b0};  // AND_Gate and_3, 8 bits wide
  assign {Cout, or_1_out} = and_1_out | and_2_out | and_3_out;  // OR_Gate or_1, 8 bits wide
  assign sum = A ^ {or_1_out, 1'b0} ^ B;  // XOR_Gate xor_1, 8 bits wide
  // Probe on sum
endmodule
