// Logisim project NSU-2023-T05L2e03.circ as structural Verilog: 2 circuits, main circuit main
module main (
  input  [7:0] A,
  output [7:0] out_2,
  output out_3
);

  wire add_1_cout, add_2_cout, add_3_cout, add_4_cout;
  wire [7:0] add_1_sum, add_2_sum, add_3_sum;

  // Probe on A
  add add_1 (.A(A), .B(A), .sum(add_1_sum), .Cout(add_1_cout));
  add add_2 (.A(add_1_sum), .B(A), .sum(add_2_sum), .Cout(add_2_cout));
  add add_3 (.A(add_2_sum), .B(A), .sum(add_3_sum), .Cout(add_3_cout));
  add add_4 (.A(add_3_sum), .B(A), .sum(out_2), .Cout(add_4_cout));
  // Probe on out_2
  or or_1 (out_3, add_4_cout, add_3_cout, add_2_cout, add_1_cout);
endmodule

module add (
  input  [7:0] A,
  input  [7:0] B,
  output [7:0] sum,
  output Cout
);

  wire [6:0] or_1_out;
  wire [7:0] and_1_out, and_2_out, and_3_out;

  assign and_1_out = A & B;  // AND_Gate and_1, 8 bits wide
  assign and_2_out = B & {or_1_out, 1'b0};  // AND_Gate and_2, 8 bits wide
  assign and_3_out = A & {or_1_out, 1'b0};  // AND_Gate and_3, 8 bits wide
  assign {Cout, or_1_out} = and_1_out | and_2_out | and_3_out;  // OR_Gate or_1, 8 bits wide
  assign sum = A ^ {or_1_out, 1'b0} ^ B;  // XOR_Gate xor_1, 8 bits wide
endmodule
