// Logisim project NSU-2023-T05L2e05.circ as structural Verilog: 2 circuits, main circuit bcd2
module bcd2 (
  input  Cin,
  input  [7:0] A,
  input  [7:0] B,
  output [7:0] R,
  output Cout
);

  wire bcd_add_2_p3;

  Hex_Digit_Display hex_digit_display_1 (.value(A[7:4]));  // open: dp
  Hex_Digit_Display hex_digit_display_2 (.value(B[7:4]));  // open: dp
  Hex_Digit_Display hex_digit_display_3 (.value({3'b000, Cin}));  // open: dp
  Hex_Digit_Display hex_digit_display_4 (.value(A[3:0]));  // open: dp
  Hex_Digit_Display hex_digit_display_5 (.value(B[3:0]));  // open: dp
  // bcd_add bcd_add_1: pin names not known; wires that end beside it: A[3:0], B[3:0], Cin, R[3:0]
  // bcd_add bcd_add_2: pin names not known; wires that end beside it: A[7:4], B[7:4], bcd_add_2_p3, Cout, R[7:4]
  Hex_Digit_Display hex_digit_display_6 (.value({3'b000, Cout}));  // open: dp
  Hex_Digit_Display hex_digit_display_7 (.value(R[7:4]));  // open: dp
  Hex_Digit_Display hex_digit_display_8 (.value(R[3:0]));  // open: dp
endmodule

// BCD
module bcd_add (
  input  [3:0] A,
  input  [3:0] B,
  input  Cin,
  output [3:0] sum,
  output Cout
);

  wire [2:0] or_1_out;
  wire [3:0] and_1_out, and_2_out, and_3_out;

  Pull_Resistor pull_resistor_1 (.node(Cin));
  assign and_1_out = A & B;  // AND_Gate and_1, 4 bits wide
  assign and_2_out = B & {or_1_out, Cin};  // AND_Gate and_2, 4 bits wide
  assign and_3_out = A & {or_1_out, Cin};  // AND_Gate and_3, 4 bits wide
  assign {Cout, or_1_out} = and_1_out | and_2_out | and_3_out;  // OR_Gate or_1, 4 bits wide
  assign sum = A ^ {or_1_out, Cin} ^ B;  // XOR_Gate xor_1, 4 bits wide
endmodule
