// Logisim project NSU-2023-T06L1e01.circ as structural Verilog: 1 circuit, main circuit fib32
module fib32 (
  input  clock,
  output [31:0] a,
  output [5:0] k,
  output stop
);

  wire clock_1_out, comparator_2_lt, or_1_out;
  wire [31:0] multiplexer_1_out, multiplexer_2_out, register_1_q, register_2_q;

  or or_1 (or_1_out, clock, clock_1_out);
  Clock clock_1 (.out(clock_1_out));
  Multiplexer #(.width(32), .enable("false")) multiplexer_1 (
    .in0(register_1_q), .in1(32'h1), .out(multiplexer_1_out), .sel(comparator_2_lt));
  Multiplexer #(.width(32), .enable("false")) multiplexer_2 (
    .in0(a), .in1({32{1'b0}}), .out(multiplexer_2_out), .sel(comparator_2_lt));
  Register #(.width(32)) register_1 (.D(multiplexer_2_out), .Q(register_1_q), .clk(or_1_out));  // open: en, clr
  Register #(.width(32)) register_2 (.D(multiplexer_1_out), .Q(register_2_q), .clk(or_1_out));  // open: en, clr
  Adder #(.width(32)) adder_1 (.a(register_1_q), .b(register_2_q), .out(a));  // open: cin, cout
  Counter #(.width(6), .max('h3f)) counter_1 (.Q(k), .clk(or_1_out));  // open: load, D, count, carry, clr
  // Probe on a
  Comparator #(.width(6)) comparator_1 (.a(k), .b(6'b101111), .eq(stop));  // open: gt, lt
  Comparator #(.width(6), .mode("unsigned")) comparator_2 (.a(k), .b(6'b000001), .lt(comparator_2_lt));  // open: gt, eq
endmodule
