// Logisim project NSU-2023-T06L1e02.circ as structural Verilog: 2 circuits, main circuit solution
module solution (
  input  [7:0] A,
  input  set,
  input  [7:0] B,
  input  clock,
  output [7:0] GCD,
  output done
);

  // Probe on A
  // Probe on B
  // Probe on GCD
endmodule

module stopper (
  input  run_prime,
  input  stop,
  input  clock_in,
  output clock_out
);

  wire multiplexer_1_out, not_1_out, or_1_out, register_1_q;

  not not_1 (not_1_out, stop);
  Multiplexer #(.enable("false")) multiplexer_1 (
    .in0(not_1_out), .in1(run_prime), .out(multiplexer_1_out), .sel(run_prime));
  or or_1 (or_1_out, run_prime, register_1_q);
  Register #(.width(1), .trigger("falling")) register_1 (
    .D(multiplexer_1_out), .en(or_1_out), .Q(register_1_q), .clk(clock_in));  // open: clr
  and and_1 (clock_out, register_1_q, clock_in);
endmodule
