// Logisim project T06L1e02.circ as structural Verilog: 2 circuits, main circuit solution
module solution (
  input  [7:0] A,
  input  set,
  input  [7:0] B,
  input  clock,
  output [7:0] GCD,
  output done
);

  wire clock_1_out, comparator_1_gt, comparator_1_lt, or_1_out, or_2_out;
  wire [7:0] B_t, multiplexer_1_out, multiplexer_2_out, multiplexer_3_out, multiplexer_4_out,
       subtractor_1_out, subtractor_2_out;

  // Probe on A
  // Probe on B
  or or_1 (or_1_out, clock, clock_1_out);
  Clock clock_1 (.out(clock_1_out));
  or or_2 (or_2_out, set, ~done);  // OR_Gate
  Multiplexer #(.width(8), .enable("false")) multiplexer_1 (
    .in0(multiplexer_3_out), .in1(A), .out(multiplexer_1_out), .sel(set));
  Multiplexer #(.width(8), .enable("false")) multiplexer_2 (
    .in0(multiplexer_4_out), .in1(B), .out(multiplexer_2_out), .sel(set));
  Register register_1 (.D(multiplexer_1_out), .en(or_2_out), .Q(GCD), .clk(or_1_out));  // open: clr
  Comparator #(.mode("unsigned")) comparator_1 (
    .a(GCD), .b(B_t), .gt(comparator_1_gt), .eq(done), .lt(comparator_1_lt));
  Register register_2 (.D(multiplexer_2_out), .en(or_2_out), .Q(B_t), .clk(or_1_out));  // open: clr
  Subtractor subtractor_1 (.a(GCD), .b(B_t), .out(subtractor_1_out));  // open: bin, bout
  Subtractor subtractor_2 (.a(B_t), .b(GCD), .out(subtractor_2_out));  // open: bin, bout
  Multiplexer #(.width(8), .enable("false")) multiplexer_3 (
    .in0(GCD), .in1(subtractor_1_out), .out(multiplexer_3_out), .sel(comparator_1_gt));
  Multiplexer #(.width(8)) multiplexer_4 (
    .in0(B_t), .in1(subtractor_2_out), .out(multiplexer_4_out), .sel(comparator_1_lt));  // open: en
  // Probe on GCD

  // Other names for the same wires on the sheet: A_t[7:0] = GCD
endmodule

module stopper (
  input  run_prime,
  input  stop,
  input  clock_in,
  output clock_out
);

  wire multiplexer_1_out, not_1_out, or_1_out, register_1_q;

  not not_1 (not_1_out, stop);
  Multiplexer #(.enable("false")) multiplexer_1 (
    .in0(not_1_out), .in1(run_prime), .out(multiplexer_1_out), .sel(run_prime));
  or or_1 (or_1_out, run_prime, register_1_q);
  Register #(.width(1), .trigger("falling")) register_1 (
    .D(multiplexer_1_out), .en(or_1_out), .Q(register_1_q), .clk(clock_in));  // open: clr
  and and_1 (clock_out, register_1_q, clock_in);
endmodule
