// Logisim project T06L1e03.circ as structural Verilog: 1 circuit, main circuit solution
module solution (
  input  A,
  input  start,
  input  clock,
  output B,
  output set
);

  wire clock_1_out, comparator_1_eq, or_1_out, or_2_out;
  wire [2:0] counter_1_q;

  Clock clock_1 (.out(clock_1_out));
  or or_1 (or_1_out, clock_1_out, clock);
  Counter #(.width(3), .max('h5)) counter_1 (
    .Q(counter_1_q), .clk(or_1_out), .clr(or_2_out));  // open: load, D, count, carry
  or or_2 (or_2_out, A, start);
  Comparator #(.width(3), .mode("unsigned")) comparator_1 (
    .a(3'b101), .b(counter_1_q), .gt(set), .eq(comparator_1_eq));  // open: lt
  or or_3 (B, A, comparator_1_eq);
endmodule
