// Logisim project NSU-2023-T06L2e01.circ as structural Verilog: 1 circuit, main circuit BBS
module BBS (
  input  [31:0] Seed,
  input  clock,
  output [31:0] Out,
  output stop
);

  wire clock_1_out, eq, or_1_out, set;
  wire [7:0] counter_1_q;
  wire [31:0] ak, multiplexer_1_out, multiplier_1_cout, multiplier_1_out, register_1_q;

  // Probe on Seed
  // Probe on 32'hb1da120d
  Multiplexer #(.width(32), .enable("false")) multiplexer_1 (.in0(Seed), .in1(ak), .out(multiplexer_1_out), .sel(set));
  Register #(.width(32)) register_1 (.D(multiplexer_1_out), .Q(register_1_q), .clk(or_1_out));  // open: en, clr
  or or_1 (or_1_out, clock, clock_1_out);
  Clock clock_1 (.out(clock_1_out));
  Multiplier #(.width(32)) multiplier_1 (
    .a(register_1_q), .b(register_1_q), .out(multiplier_1_out), .cout(multiplier_1_cout));  // open: cin
  Counter counter_1 (.Q(counter_1_q), .clk(or_1_out));  // open: load, D, count, carry, clr
  Divider #(.width(32)) divider_1 (
    .a(multiplier_1_out), .b(32'hb1da120d), .upper(multiplier_1_cout), .rem(ak));  // open: out
  Comparator #(.mode("unsigned")) comparator_1 (.a({8{1'b0}}), .b(counter_1_q), .eq(eq), .lt(set));  // open: gt
  Multiplexer #(.width(32)) multiplexer_2 (.in0(ak), .in1(Seed), .out(Out), .sel(eq));  // open: en
  Comparator #(.mode("unsigned")) comparator_2 (.a(counter_1_q), .b(8'hf), .eq(stop));  // open: gt, lt
  // Probe on Out

  // Other names for the same wires on the sheet: x[31:0] = Seed
endmodule
